// Logisim project EP2finalizad.circ as structural Verilog
module main (
  input  [7:0] A,
  input  [7:0] B,
  input  OP,
  output C0,
  output C1,
  output C2,
  output C3,
  output C4,
  output C5,
  output [7:0] R,
  output overflow_com_sinal,
  output overflow_sem_sinal
);

  comparador comparador_1 (.A(A), .B(B), .C0(C0), .C2(C2), .C1(C1));
  VERIFICA_0 verifica_0_1 (.A(A), .C3(C3));
  ULA ula_1 (
    .A(A), .B(B), .OVERFLOW_COM_SINAL(overflow_com_sinal), .RESULTADO(R),
    .OVERFLOW_SEM_FINAL(overflow_sem_sinal), .OP(OP), .C4(C4), .C5(C5));
endmodule

module somabit (
  input  A,
  input  B,
  input  cin,
  output s,
  output cout
);

  wire and_1_out, and_2_out, xor_1_out;

  xor xor_1 (xor_1_out, A, B);
  xor xor_2 (s, xor_1_out, cin);
  and and_1 (and_1_out, xor_1_out, cin);
  and and_2 (and_2_out, A, B);
  or or_1 (cout, and_1_out, and_2_out);
endmodule

module ULA (
  input  [7:0] A,
  input  OP,
  input  [7:0] B,
  output OVERFLOW_COM_SINAL,
  output [7:0] RESULTADO,
  output OVERFLOW_SEM_FINAL,
  output C4,
  output C5
);

  wire and_1_out, and_2_out, and_3_out, and_4_out, and_5_out, and_6_out, and_7_out, and_8_out, and_9_out,
       and_10_out, and_11_out, and_12_out, and_13_out, and_14_out, and_15_out, and_16_out, comparabits_1_c0,
       comparabits_1_c1, comparabits_1_c2, comparabits_2_c0, comparabits_2_c1, comparabits_2_c2,
       comparabits_3_c0, comparabits_3_c1, comparabits_3_c2, comparabits_4_c0, comparabits_4_c1,
       comparabits_4_c2, comparabits_5_c0, comparabits_5_c2, comparabits_6_c0, comparabits_6_c1,
       comparabits_6_c2, comparabits_7_c0, comparabits_7_c1, comparabits_7_c2, comparabits_8_c0,
       comparabits_8_c1, comparabits_8_c2, comparabits_9_c0, comparabits_9_c1, comparabits_9_c2,
       comparabits_10_c0, comparabits_10_c1, comparabits_10_c2, comparabits_11_c0, comparabits_11_c1,
       comparabits_11_c2, comparabits_12_c0, comparabits_12_c1, comparabits_12_c2, comparabits_13_c0,
       comparabits_13_c1, comparabits_13_c2, comparabits_14_c0, comparabits_14_c1, comparabits_14_c2,
       comparabits_15_c0, comparabits_15_c1, comparabits_15_c2, comparabits_16_c0, comparabits_16_c1,
       comparabits_16_c2, somabit_1_cout, somabit_2_cout, somabit_3_cout, somabit_4_cout, somabit_5_cout,
       somabit_6_cout, somabit_7_cout, somabit_8_cout;
  wire [7:0] multiplexer_1_out, not_1_out;

  assign not_1_out = ~B;  // NOT_Gate not_1, 8 bits wide
  somabit somabit_1 (.A(A[7]), .B(multiplexer_1_out[7]), .s(RESULTADO[7]), .cout(somabit_1_cout), .cin(somabit_2_cout));
  COMPARABITS comparabits_1 (
    .A(A[7]), .B(multiplexer_1_out[7]), .ATIVAR(1'b1), .C0(comparabits_1_c0), .C1(comparabits_1_c1),
    .C2(comparabits_1_c2));
  somabit somabit_2 (.A(A[6]), .B(multiplexer_1_out[6]), .s(RESULTADO[6]), .cout(somabit_2_cout), .cin(somabit_3_cout));
  COMPARABITS comparabits_2 (
    .A(A[6]), .B(multiplexer_1_out[6]), .ATIVAR(comparabits_3_c2), .C0(comparabits_2_c0),
    .C1(comparabits_2_c1), .C2(comparabits_2_c2));
  COMPARABITS comparabits_3 (
    .A(A[7]), .B(multiplexer_1_out[7]), .ATIVAR(comparabits_1_c2), .C0(comparabits_3_c0),
    .C1(comparabits_3_c1), .C2(comparabits_3_c2));
  somabit somabit_3 (.A(A[5]), .B(multiplexer_1_out[5]), .s(RESULTADO[5]), .cout(somabit_3_cout), .cin(somabit_4_cout));
  Multiplexer #(.width(8), .enable("false")) multiplexer_1 (
    .in0(B), .in1(not_1_out), .out(multiplexer_1_out), .sel(OP));
  COMPARABITS comparabits_4 (
    .A(A[5]), .B(multiplexer_1_out[5]), .ATIVAR(comparabits_5_c2), .C0(comparabits_4_c0),
    .C1(comparabits_4_c1), .C2(comparabits_4_c2));
  COMPARABITS comparabits_5 (
    .A(A[6]), .B(multiplexer_1_out[6]), .ATIVAR(comparabits_2_c2), .C0(comparabits_5_c0),
    .C1(comparabits_3_c1), .C2(comparabits_5_c2));
  somabit somabit_4 (.A(A[4]), .B(multiplexer_1_out[4]), .s(RESULTADO[4]), .cout(somabit_4_cout), .cin(somabit_5_cout));
  COMPARABITS comparabits_6 (
    .A(A[5]), .B(multiplexer_1_out[5]), .ATIVAR(comparabits_4_c2), .C0(comparabits_6_c0),
    .C1(comparabits_6_c1), .C2(comparabits_6_c2));
  COMPARABITS comparabits_7 (
    .A(A[4]), .B(multiplexer_1_out[4]), .ATIVAR(comparabits_6_c2), .C0(comparabits_7_c0),
    .C1(comparabits_7_c1), .C2(comparabits_7_c2));
  somabit somabit_5 (.A(A[3]), .B(multiplexer_1_out[3]), .s(RESULTADO[3]), .cout(somabit_5_cout), .cin(somabit_6_cout));
  COMPARABITS comparabits_8 (
    .A(A[3]), .B(multiplexer_1_out[3]), .ATIVAR(comparabits_9_c2), .C0(comparabits_8_c0),
    .C1(comparabits_8_c1), .C2(comparabits_8_c2));
  COMPARABITS comparabits_9 (
    .A(A[4]), .B(multiplexer_1_out[4]), .ATIVAR(comparabits_7_c2), .C0(comparabits_9_c0),
    .C1(comparabits_9_c1), .C2(comparabits_9_c2));
  somabit somabit_6 (.A(A[2]), .B(multiplexer_1_out[2]), .s(RESULTADO[2]), .cout(somabit_6_cout), .cin(somabit_7_cout));
  COMPARABITS comparabits_10 (
    .A(A[2]), .B(multiplexer_1_out[2]), .ATIVAR(comparabits_11_c2), .C0(comparabits_10_c0),
    .C1(comparabits_10_c1), .C2(comparabits_10_c2));
  COMPARABITS comparabits_11 (
    .A(A[2]), .B(multiplexer_1_out[2]), .ATIVAR(comparabits_8_c2), .C0(comparabits_11_c0),
    .C1(comparabits_11_c1), .C2(comparabits_11_c2));
  somabit somabit_7 (.A(A[1]), .B(multiplexer_1_out[1]), .s(RESULTADO[1]), .cout(somabit_7_cout), .cin(somabit_8_cout));
  COMPARABITS comparabits_12 (
    .A(A[1]), .B(multiplexer_1_out[1]), .ATIVAR(comparabits_13_c2), .C0(comparabits_12_c0),
    .C1(comparabits_12_c1), .C2(comparabits_12_c2));
  COMPARABITS comparabits_13 (
    .A(A[1]), .B(multiplexer_1_out[1]), .ATIVAR(comparabits_10_c2), .C0(comparabits_13_c0),
    .C1(comparabits_13_c1), .C2(comparabits_13_c2));
  somabit somabit_8 (.A(A[0]), .B(multiplexer_1_out[0]), .s(RESULTADO[0]), .cout(somabit_8_cout), .cin(OP));
  COMPARABITS comparabits_14 (
    .A(A[0]), .B(multiplexer_1_out[0]), .ATIVAR(comparabits_15_c2), .C0(comparabits_14_c0),
    .C1(comparabits_14_c1), .C2(comparabits_14_c2));
  COMPARABITS comparabits_15 (
    .A(A[0]), .B(multiplexer_1_out[0]), .ATIVAR(comparabits_12_c2), .C0(comparabits_15_c0),
    .C1(comparabits_15_c1), .C2(comparabits_15_c2));
  xnor xnor_1 (OVERFLOW_COM_SINAL, RESULTADO[7], RESULTADO[6]);
  xor xor_1 (OVERFLOW_SEM_FINAL, somabit_1_cout, OP);
  COMPARABITS comparabits_16 (
    .A(RESULTADO[0]), .B(somabit_8_cout), .ATIVAR(comparabits_14_c2), .C0(comparabits_16_c0),
    .C1(comparabits_16_c1), .C2(comparabits_16_c2));
  and and_1 (and_1_out, comparabits_1_c0, ~comparabits_1_c1);  // AND_Gate
  and and_2 (and_2_out, comparabits_2_c0, ~comparabits_2_c1);  // AND_Gate
  and and_3 (and_3_out, comparabits_4_c0, ~comparabits_4_c1);  // AND_Gate
  and and_4 (and_4_out, comparabits_7_c0, ~comparabits_7_c1);  // AND_Gate
  and and_5 (and_5_out, comparabits_8_c0, ~comparabits_8_c1);  // AND_Gate
  and and_6 (and_6_out, comparabits_10_c0, ~comparabits_10_c1);  // AND_Gate
  and and_7 (and_7_out, comparabits_12_c0, ~comparabits_12_c1);  // AND_Gate
  and and_8 (and_8_out, comparabits_14_c0, ~comparabits_14_c1);  // AND_Gate
  and and_9 (and_9_out, ~comparabits_3_c0, comparabits_3_c1);  // AND_Gate
  and and_10 (and_10_out, ~comparabits_5_c0, comparabits_3_c1);  // AND_Gate
  and and_11 (and_11_out, ~comparabits_6_c0, comparabits_6_c1);  // AND_Gate
  and and_12 (and_12_out, ~comparabits_9_c0, comparabits_9_c1);  // AND_Gate
  and and_13 (and_13_out, ~comparabits_11_c0, comparabits_11_c1);  // AND_Gate
  and and_14 (and_14_out, ~comparabits_13_c0, comparabits_13_c1);  // AND_Gate
  and and_15 (and_15_out, ~comparabits_15_c0, comparabits_15_c1);  // AND_Gate
  and and_16 (and_16_out, ~comparabits_16_c0, comparabits_16_c1);  // AND_Gate
  or or_1 (C4, and_1_out, and_2_out, and_3_out, and_4_out, and_5_out, and_6_out, and_7_out, and_8_out);
  or or_2 (C5, and_9_out, and_10_out, and_11_out, and_12_out, and_13_out, and_14_out, and_15_out, and_16_out);
endmodule

module COMPARABITS (
  input  A,
  input  B,
  input  ATIVAR,
  output C0,
  output C1,
  output C2
);

  wire and_1_out, and_2_out, xnor_1_out;

  and and_1 (and_1_out, A, ~B);  // AND_Gate
  and and_2 (and_2_out, ~A, B);  // AND_Gate
  xnor xnor_1 (xnor_1_out, A, B);
  and and_3 (C0, and_1_out, ATIVAR);
  and and_4 (C1, and_2_out, ATIVAR);
  and and_5 (C2, xnor_1_out, ATIVAR);
endmodule

module comparador (
  input  [7:0] A,
  input  [7:0] B,
  output C0,
  output C2,
  output C1
);

  wire comparabits_1_c0, comparabits_1_c2, comparabits_2_c0, comparabits_2_c2, comparabits_3_c0,
       comparabits_3_c2, comparabits_4_c0, comparabits_4_c2, comparabits_5_c0, comparabits_5_c2,
       comparabits_6_c0, comparabits_6_c2, comparabits_7_c0, comparabits_7_c2, comparabits_8_c0;

  COMPARABITS comparabits_1 (
    .A(A[7]), .B(B[7]), .ATIVAR(1'b1), .C0(comparabits_1_c0), .C2(comparabits_1_c2));  // open: C1
  COMPARABITS comparabits_2 (
    .A(A[6]), .B(B[6]), .ATIVAR(comparabits_1_c2), .C0(comparabits_2_c0), .C2(comparabits_2_c2));  // open: C1
  COMPARABITS comparabits_3 (
    .A(A[5]), .B(B[5]), .ATIVAR(comparabits_2_c2), .C0(comparabits_3_c0), .C2(comparabits_3_c2));  // open: C1
  or or_1 (C0, comparabits_1_c0, comparabits_2_c0, comparabits_3_c0, comparabits_4_c0, comparabits_5_c0, comparabits_6_c0, comparabits_7_c0, comparabits_8_c0);
  COMPARABITS comparabits_4 (
    .A(A[4]), .B(B[4]), .ATIVAR(comparabits_3_c2), .C0(comparabits_4_c0), .C2(comparabits_4_c2));  // open: C1
  COMPARABITS comparabits_5 (
    .A(A[3]), .B(B[3]), .ATIVAR(comparabits_4_c2), .C0(comparabits_5_c0), .C2(comparabits_5_c2));  // open: C1
  COMPARABITS comparabits_6 (
    .A(B[2]), .B(A[2]), .ATIVAR(comparabits_5_c2), .C0(comparabits_6_c0), .C2(comparabits_6_c2));  // open: C1
  COMPARABITS comparabits_7 (
    .A(A[1]), .B(B[1]), .ATIVAR(comparabits_6_c2), .C0(comparabits_7_c0), .C2(comparabits_7_c2));  // open: C1
  COMPARABITS comparabits_8 (
    .A(A[0]), .B(B[0]), .ATIVAR(comparabits_7_c2), .C0(comparabits_8_c0), .C2(C2));  // open: C1
  and and_1 (C1, ~C0, ~C2);  // AND_Gate
endmodule

module VERIFICA_0 (
  input  [7:0] A,
  output C3
);

  and and_1 (C3, ~A[7], ~A[6], ~A[5], ~A[4], ~A[3], ~A[2], ~A[1], ~A[0]);  // AND_Gate
endmodule
